// Logisim project scheme_log.circ as structural Verilog: 1 circuit, main circuit main
module main (
  input  \А1 ,
  input  A2,
  input  B1,
  input  B2,
  input  B3,
  input  C,
  input  in_7
);

  wire A2_nB1_out, A2B1C_out, and_1_out, and_2_out, and_3_out, and_4_out, and_5_out, and_6_out, and_7_out,
       and_8_out, and_9_out, nA2_nB2B3_nC_out, nA2B2_out, not_1_out, not_2_out, not_3_out, not_4_out,
       not_5_out, not_6_out, or_1_out, or_2_out, Q0_q, Q0_qn, Q1_q, Q1_qn;

  and A2_nB1 (A2_nB1_out, A2, not_1_out);
  not not_1 (not_1_out, B1);
  not not_2 (not_2_out, A2);
  and nA2B2 (nA2B2_out, not_2_out, B2);
  and A2B1C (A2B1C_out, A2, B1, C);
  not not_3 (not_3_out, A2);
  not not_4 (not_4_out, B2);
  and nA2_nB2B3_nC (nA2_nB2B3_nC_out, not_3_out, not_4_out, B3, not_5_out);
  not not_5 (not_5_out, C);
  not not_6 (not_6_out, C);
  or or_1 (or_1_out, A2_nB1_out, nA2B2_out, A2B1C_out, nA2_nB2B3_nC_out);
  and and_1 (and_1_out, or_1_out, \А1 );
  and and_2 (and_2_out, Q0_qn, Q1_qn);
  and and_3 (and_3_out, and_2_out, and_1_out);
  and and_4 (and_4_out, Q1_q, Q1_q, Q0_qn);
  and and_5 (and_5_out, Q1_q, Q0_qn);
  or or_2 (or_2_out, and_6_out, and_3_out);
  D_Flip_Flop Q1 (.clk(in_7), .D(or_2_out), .Q(Q1_q), .Qn(Q1_qn));  // open: preset, en, reset
  and and_6 (and_6_out, and_5_out, not_6_out);
  D_Flip_Flop Q0 (.clk(in_7), .D(and_4_out), .Q(Q0_q), .Qn(Q0_qn));  // open: preset, en, reset
  and and_7 (and_7_out, Q1_q, Q0_q);
  and and_8 (and_8_out, Q1_qn, Q0_q);
  and and_9 (and_9_out, Q1_q, Q0_qn);

  // Notes on the sheet:
  //   S3
  //   S2
  //   S1
endmodule
